# Fritzing sketch ESP32_SenseAirS8 (saved by Fritzing 0.9.3b)
circuit board: 9.61871cm x 6.76387cm

parts:
  ES1 = ESP32 DEVKIT 38 pins
  SA1 = SenseAirS8 CO2 sensor
  DHT1 = DHT22 Sensor
  OL1 = OLED 0.96" 128x64 I2C SSD1306
  R1 = Resistor [tolerance=±5% resistance=10k package=THT]
  C1 = Electrolytic Capacitor [capacitance=470µF package="100 mil [THT, electrolytic]"]
  C2 = Electrolytic Capacitor [capacitance=220µF package="100 mil [THT, electrolytic]"]

nets:
  VCC: ES1.3V3, DHT1.Vcc, OL1.VCC, R1.Pin_0, C1.+
  5V: ES1.5V, SA1.Vin, C2.+
  GND: ES1.GND, SA1.GND, DHT1.GND_2, OL1.GND, C1.-, C2.-
  N1: ES1.IO22, OL1.SCL
  N2: ES1.IO21, OL1.SCA
  N3: ES1.IO19, DHT1.Data-signal, R1.Pin_1
  N4: ES1.IO17, SA1.RX
  N5: ES1.IO16, SA1.TX

custom parts:
  ESP32 DEVKIT 38 pins: github.com/AlexVakhnin
